// Logisim project ULA_8_BITS.circ as structural Verilog: 8 circuits, main circuit main
module main (
  input  [7:0] in_1,
  input  [7:0] in_2,
  input  [3:0] in_3,
  output [7:0] out_4,
  output out_5,
  output out_6
);

  ULA_8BITS ula_8bits_1 (
    .A(in_1), .B(in_2), .\saída (out_4), .overflow_sub(out_5), .overflow_sum(out_6), .ula_seletor(in_3));

  // Notes on the sheet:
  //   SHIFT LEFT(2b)
  //   SHIFT RIGHT(2b)
  //   SOMADOR
  //   OPERAÇÕES
  //   AND
  //   OR
  //   NOT(A)
  //   NOR
  //   NAND
  //   XOR
  //   SUB
  //   shift left, shift right
  //   e not são aplicadas na entrada A
  //   0001
  //   0010
  //   0011
  //   0100
  //   0101
  //   0110
  //   0111
  //   1000
  //   1001
  //   1010
endmodule

module ULA_8BITS (
  input  [7:0] A,
  input  [7:0] B,
  input  [3:0] ula_seletor,
  output [7:0] \saída ,
  output overflow_sub,
  output overflow_sum
);

  wire [7:0] \and_8bits_1_saída , \nand_8bits_1_saída , \nor_8bits_1_saída , \not_8bits_1_saída ,
       \or_8bits_1_saída , shift_2_1_left, shift_2_1_right, somador_8_bits_1_s, \subtrator_1_saída ,
       \xor_8bits_1_saída ;

  AND_8bits and_8bits_1 (.\SAÍDA (\and_8bits_1_saída ), .A(A), .B(B));
  OR_8bits or_8bits_1 (.\SAÍDA (\or_8bits_1_saída ), .A(A), .B(B));
  NOT_8bits not_8bits_1 (.\SAÍDA (\not_8bits_1_saída ), .A(A));
  NOR_8bits nor_8bits_1 (.\SAÍDA (\nor_8bits_1_saída ), .A(A), .B(B));
  NAND_8bits nand_8bits_1 (.\SAÍDA (\nand_8bits_1_saída ), .A(A), .B(B));
  XOR_8bits xor_8bits_1 (.\SAÍDA (\xor_8bits_1_saída ), .A(A), .B(B));
  subtrator subtrator_1 (.\SAÍDA (\subtrator_1_saída ), .OVERFLOW(overflow_sub), .A(A), .B(B));
  shift_2 shift_2_1 (.entrada(A), .LEFT(shift_2_1_left), .RIGHT(shift_2_1_right));
  somador_8_bits somador_8_bits_1 (.A(A), .B(B), .S(somador_8_bits_1_s), .overflow(overflow_sum));
  Multiplexer #(.select(4), .width(8)) multiplexer_1 (
    .in1(\and_8bits_1_saída ), .in2(\or_8bits_1_saída ), .in3(\not_8bits_1_saída ),
    .in4(\nor_8bits_1_saída ), .in5(\nand_8bits_1_saída ), .in6(\xor_8bits_1_saída ),
    .in7(\subtrator_1_saída ), .in8(shift_2_1_left), .in9(shift_2_1_right), .in10(somador_8_bits_1_s),
    .out(\saída ), .sel(ula_seletor));  // open: in0, in11, in12, in13, in14, in15, en

  // Notes on the sheet:
  //   SUB
  //   shift
  //   2 bits
  //   SUM
endmodule

// AND
module AND_8bits (
  input  [7:0] A,
  input  [7:0] B,
  output [7:0] \SAÍDA 
);

  and and_1 (\SAÍDA [0], B[0], A[0]);
  and and_2 (\SAÍDA [1], B[1], A[1]);
  and and_3 (\SAÍDA [2], B[2], A[2]);
  and and_4 (\SAÍDA [3], B[3], A[3]);
  and and_5 (\SAÍDA [4], B[4], A[4]);
  and and_6 (\SAÍDA [5], B[5], A[5]);
  and and_7 (\SAÍDA [6], B[6], A[6]);
  and and_8 (\SAÍDA [7], B[7], A[7]);
endmodule

// OR
module OR_8bits (
  input  [7:0] A,
  input  [7:0] B,
  output [7:0] \SAÍDA 
);

  or or_1 (\SAÍDA [0], B[0], A[0]);
  or or_2 (\SAÍDA [1], B[1], A[1]);
  or or_3 (\SAÍDA [2], B[2], A[2]);
  or or_4 (\SAÍDA [3], B[3], A[3]);
  or or_5 (\SAÍDA [4], B[4], A[4]);
  or or_6 (\SAÍDA [5], B[5], A[5]);
  or or_7 (\SAÍDA [6], B[6], A[6]);
  or or_8 (\SAÍDA [7], B[7], A[7]);
endmodule

// NOT
module NOT_8bits (
  input  [7:0] A,
  output [7:0] \SAÍDA 
);

  assign \SAÍDA  = ~A;  // NOT_Gate not_1, 8 bits wide
endmodule

// NOR
module NOR_8bits (
  input  [7:0] A,
  input  [7:0] B,
  output [7:0] \SAÍDA 
);

  nor nor_1 (\SAÍDA [0], B[0], A[0]);
  nor nor_2 (\SAÍDA [1], B[1], A[1]);
  nor nor_3 (\SAÍDA [2], B[2], A[2]);
  nor nor_4 (\SAÍDA [3], B[3], A[3]);
  nor nor_5 (\SAÍDA [4], B[4], A[4]);
  nor nor_6 (\SAÍDA [5], B[5], A[5]);
  nor nor_7 (\SAÍDA [6], B[6], A[6]);
  nor nor_8 (\SAÍDA [7], B[7], A[7]);
endmodule

// NAND
module NAND_8bits (
  input  [7:0] A,
  input  [7:0] B,
  output [7:0] \SAÍDA 
);

  nand nand_1 (\SAÍDA [0], B[0], A[0]);
  nand nand_2 (\SAÍDA [1], B[1], A[1]);
  nand nand_3 (\SAÍDA [2], B[2], A[2]);
  nand nand_4 (\SAÍDA [3], B[3], A[3]);
  nand nand_5 (\SAÍDA [4], B[4], A[4]);
  nand nand_6 (\SAÍDA [5], B[5], A[5]);
  nand nand_7 (\SAÍDA [6], B[6], A[6]);
  nand nand_8 (\SAÍDA [7], B[7], A[7]);
endmodule

// XOR
module XOR_8bits (
  input  [7:0] A,
  input  [7:0] B,
  output [7:0] \SAÍDA 
);

  xor xor_1 (\SAÍDA [0], B[0], A[0]);
  xor xor_2 (\SAÍDA [1], B[1], A[1]);
  xor xor_3 (\SAÍDA [2], B[2], A[2]);
  xor xor_4 (\SAÍDA [3], B[3], A[3]);
  xor xor_5 (\SAÍDA [4], B[4], A[4]);
  xor xor_6 (\SAÍDA [5], B[5], A[5]);
  xor xor_7 (\SAÍDA [6], B[6], A[6]);
  xor xor_8 (\SAÍDA [7], B[7], A[7]);
endmodule
