// Logisim project banco_registradores.circ as structural Verilog: 2 circuits, main circuit main
module main (
  input  [3:0] in_1,
  input  [7:0] in_2,
  input  in_3,
  input  [3:0] in_4,
  input  [3:0] in_5,
  output [7:0] out_6,
  output [7:0] out_7
);

  banco_registradores banco_registradores_1 (
    .data_in(in_2), .write(in_3), .write_select(in_1), .rx(out_6), .rx_select(in_4), .ry(out_7),
    .ry_select(in_5));
endmodule

module banco_registradores (
  input  [3:0] rx_select,
  input  [3:0] ry_select,
  input  [7:0] data_in,
  input  write,
  input  [3:0] write_select,
  output [7:0] rx,
  output [7:0] ry
);

  wire demultiplexer_1_out0, demultiplexer_1_out1, demultiplexer_1_out2, demultiplexer_1_out3,
       demultiplexer_1_out4, demultiplexer_1_out5, demultiplexer_1_out6, demultiplexer_1_out7,
       demultiplexer_1_out8, demultiplexer_1_out9, demultiplexer_1_out10, demultiplexer_1_out11,
       demultiplexer_1_out12, demultiplexer_1_out13, demultiplexer_1_out14, demultiplexer_1_out15;
  wire [7:0] \registrador_1_saída , \registrador_2_saída , \registrador_3_saída , \registrador_4_saída ,
       \registrador_5_saída , \registrador_6_saída , \registrador_7_saída , \registrador_8_saída ,
       \registrador_9_saída , \registrador_10_saída , \registrador_11_saída , \registrador_12_saída ,
       \registrador_13_saída , \registrador_14_saída , \registrador_15_saída , \registrador_16_saída ;

  Demultiplexer #(.select(4)) demultiplexer_1 (
    .out0(demultiplexer_1_out0), .out1(demultiplexer_1_out1), .out2(demultiplexer_1_out2),
    .out3(demultiplexer_1_out3), .out4(demultiplexer_1_out4), .out5(demultiplexer_1_out5),
    .out6(demultiplexer_1_out6), .out7(demultiplexer_1_out7), .out8(demultiplexer_1_out8),
    .out9(demultiplexer_1_out9), .out10(demultiplexer_1_out10), .out11(demultiplexer_1_out11),
    .out12(demultiplexer_1_out12), .out13(demultiplexer_1_out13), .out14(demultiplexer_1_out14),
    .out15(demultiplexer_1_out15), .in(write), .sel(write_select));  // open: en
  registrador registrador_1 (.entrada(data_in), .\saída (\registrador_1_saída ), .CLOCK(demultiplexer_1_out0));
  registrador registrador_2 (.entrada(data_in), .\saída (\registrador_2_saída ), .CLOCK(demultiplexer_1_out1));
  registrador registrador_3 (.entrada(data_in), .\saída (\registrador_3_saída ), .CLOCK(demultiplexer_1_out2));
  registrador registrador_4 (.entrada(data_in), .\saída (\registrador_4_saída ), .CLOCK(demultiplexer_1_out3));
  registrador registrador_5 (.entrada(data_in), .\saída (\registrador_5_saída ), .CLOCK(demultiplexer_1_out4));
  registrador registrador_6 (.entrada(data_in), .\saída (\registrador_6_saída ), .CLOCK(demultiplexer_1_out5));
  registrador registrador_7 (.entrada(data_in), .\saída (\registrador_7_saída ), .CLOCK(demultiplexer_1_out6));
  registrador registrador_8 (.entrada(data_in), .\saída (\registrador_8_saída ), .CLOCK(demultiplexer_1_out7));
  registrador registrador_9 (.entrada(data_in), .\saída (\registrador_9_saída ), .CLOCK(demultiplexer_1_out8));
  registrador registrador_10 (.entrada(data_in), .\saída (\registrador_10_saída ), .CLOCK(demultiplexer_1_out9));
  registrador registrador_11 (.entrada(data_in), .\saída (\registrador_11_saída ), .CLOCK(demultiplexer_1_out10));
  registrador registrador_12 (.entrada(data_in), .\saída (\registrador_12_saída ), .CLOCK(demultiplexer_1_out11));
  registrador registrador_13 (.entrada(data_in), .\saída (\registrador_13_saída ), .CLOCK(demultiplexer_1_out12));
  registrador registrador_14 (.entrada(data_in), .\saída (\registrador_14_saída ), .CLOCK(demultiplexer_1_out13));
  registrador registrador_15 (.entrada(data_in), .\saída (\registrador_15_saída ), .CLOCK(demultiplexer_1_out14));
  registrador registrador_16 (.entrada(data_in), .\saída (\registrador_16_saída ), .CLOCK(demultiplexer_1_out15));
  Multiplexer #(.select(4), .width(8)) multiplexer_1 (
    .in0(\registrador_1_saída ), .in1(\registrador_2_saída ), .in2(\registrador_3_saída ),
    .in3(\registrador_4_saída ), .in4(\registrador_5_saída ), .in5(\registrador_6_saída ),
    .in6(\registrador_7_saída ), .in7(\registrador_8_saída ), .in8(\registrador_9_saída ),
    .in9(\registrador_10_saída ), .in10(\registrador_11_saída ), .in11(\registrador_12_saída ),
    .in12(\registrador_13_saída ), .in13(\registrador_14_saída ), .in14(\registrador_15_saída ),
    .in15(\registrador_16_saída ), .out(rx), .sel(rx_select));  // open: en
  Multiplexer #(.select(4), .width(8)) multiplexer_2 (
    .in0(\registrador_1_saída ), .in1(\registrador_2_saída ), .in2(\registrador_3_saída ),
    .in3(\registrador_4_saída ), .in4(\registrador_5_saída ), .in5(\registrador_6_saída ),
    .in6(\registrador_7_saída ), .in7(\registrador_8_saída ), .in8(\registrador_9_saída ),
    .in9(\registrador_10_saída ), .in10(\registrador_11_saída ), .in11(\registrador_12_saída ),
    .in12(\registrador_13_saída ), .in13(\registrador_14_saída ), .in14(\registrador_15_saída ),
    .in15(\registrador_16_saída ), .out(ry), .sel(ry_select));  // open: en
endmodule
