// Logisim project contador_sincrono.circ as structural Verilog: 2 circuits, main circuit main
module main (
  output [3:0] out_1
);

  wire clock_1_out;

  Clock clock_1 (.out(clock_1_out));
  contador_sincrono contador_sincrono_1 (.CLOCK(clock_1_out), .\SAÍDA (out_1));
endmodule

module contador_sincrono (
  input  CLOCK,
  output [3:0] \SAÍDA 
);

  wire and_1_out, and_2_out, d_ff_1_qn, xor_1_out, xor_2_out, xor_3_out;

  D_Flip_Flop d_ff_1 (.clk(CLOCK), .D(d_ff_1_qn), .Q(\SAÍDA [0]), .Qn(d_ff_1_qn));  // open: preset, en, reset
  D_Flip_Flop d_ff_2 (.clk(CLOCK), .D(xor_1_out), .Q(\SAÍDA [1]));  // open: Qn, preset, en, reset
  D_Flip_Flop d_ff_3 (.clk(CLOCK), .D(xor_2_out), .Q(\SAÍDA [2]));  // open: Qn, preset, en, reset
  D_Flip_Flop d_ff_4 (.clk(CLOCK), .D(xor_3_out), .Q(\SAÍDA [3]));  // open: Qn, preset, en, reset
  xor xor_1 (xor_1_out, \SAÍDA [0], \SAÍDA [1]);
  and and_1 (and_1_out, \SAÍDA [1], \SAÍDA [0]);
  xor xor_2 (xor_2_out, \SAÍDA [2], and_1_out);
  and and_2 (and_2_out, \SAÍDA [2], \SAÍDA [1], \SAÍDA [0]);
  xor xor_3 (xor_3_out, \SAÍDA [3], and_2_out);
endmodule
