// Logisim project detector_numero_primo.circ as structural Verilog: 2 circuits, main circuit main
module main (
  input  [3:0] in_1,
  output \saída 
);

  detector_num_primo detector_num_primo_1 (.\SAÍDA (\saída ), .ENTRADA(in_1));
endmodule

module detector_num_primo (
  input  [3:0] ENTRADA,
  output \SAÍDA 
);

  wire and_1_out, and_2_out, and_3_out, and_4_out;

  and and_1 (and_1_out, ~ENTRADA[3], ~ENTRADA[2], ENTRADA[1]);  // AND_Gate
  and and_2 (and_2_out, ENTRADA[2], ~ENTRADA[1], ENTRADA[0]);  // AND_Gate
  and and_3 (and_3_out, ~ENTRADA[2], ENTRADA[1], ENTRADA[0]);  // AND_Gate
  and and_4 (and_4_out, ~ENTRADA[3], ENTRADA[2], ENTRADA[0]);  // AND_Gate
  or or_1 (\SAÍDA , and_1_out, and_2_out, and_3_out, and_4_out);
endmodule
