// Logisim project detector_paridade_impar.circ as structural Verilog: 2 circuits, main circuit main
module main (
  input  [3:0] in_1,
  output out_2
);

  detector_paridade_impar detector_paridade_impar_1 (.out_2(out_2), .entrada(in_1));
endmodule

module detector_paridade_impar (
  input  [3:0] entrada,
  output out_2
);

  wire and_1_out, and_2_out, and_3_out, and_4_out, and_5_out, and_6_out, and_7_out, and_8_out;

  and and_1 (and_1_out, entrada[3], ~entrada[2], ~entrada[1], ~entrada[0]);  // AND_Gate
  and and_2 (and_2_out, ~entrada[3], entrada[2], ~entrada[1], ~entrada[0]);  // AND_Gate
  and and_3 (and_3_out, ~entrada[3], ~entrada[2], entrada[1], ~entrada[0]);  // AND_Gate
  and and_4 (and_4_out, ~entrada[3], ~entrada[2], ~entrada[1], entrada[0]);  // AND_Gate
  and and_5 (and_5_out, entrada[3], entrada[2], entrada[1], ~entrada[0]);  // AND_Gate
  and and_6 (and_6_out, entrada[3], entrada[2], ~entrada[1], entrada[0]);  // AND_Gate
  and and_7 (and_7_out, entrada[3], ~entrada[2], entrada[1], entrada[0]);  // AND_Gate
  and and_8 (and_8_out, ~entrada[3], entrada[2], entrada[1], entrada[0]);  // AND_Gate
  or or_1 (out_2, and_1_out, and_2_out, and_3_out, and_4_out, and_5_out, and_6_out, and_7_out, and_8_out);
endmodule
