// Logisim project detector_sequencia.circ as structural Verilog: 2 circuits, main circuit main
module main (
  input  in_1,
  output out_2
);

  wire clock_1_out;

  detector_sequencia_101 detector_sequencia_101_1 (.ENTRADA(in_1), .\saída (out_2), .clock(clock_1_out));
  Clock clock_1 (.out(clock_1_out));
endmodule

module detector_sequencia_101 (
  input  clock,
  input  ENTRADA,
  output \saída 
);

  wire and_1_out, d0_q, d1_q, not_1_out;

  D_Flip_Flop d0 (.clk(clock), .D(ENTRADA), .Q(d0_q));  // open: Qn, preset, en, reset
  not not_1 (not_1_out, ENTRADA);
  D_Flip_Flop d1 (.clk(clock), .D(and_1_out), .Q(d1_q));  // open: Qn, preset, en, reset
  and and_1 (and_1_out, d0_q, not_1_out);
  and and_2 (\saída , d1_q, ENTRADA);
endmodule
