// Logisim project extensor_sinal_4_8.circ as structural Verilog: 2 circuits, main circuit main
module main (
  input  [3:0] in_1,
  output [7:0] out_2
);

  extensor_sinal extensor_sinal_1 (.\saída (out_2), .entrada(in_1));
endmodule

module extensor_sinal (
  input  [3:0] entrada,
  output [7:0] \saída 
);


  assign \saída  = {{5{entrada[3]}}, entrada[2:0]};
endmodule
