// Logisim project flip_flop_d.circ as structural Verilog: 2 circuits, main circuit main
module main (
  input  in_1,
  output out_2,
  output out_3
);

  wire clock_1_out;

  Clock clock_1 (.out(clock_1_out));
  FLIP_FLOP_D flip_flop_d_1 (.D(in_1), .CLOCK(clock_1_out), .Q(out_2), .nQ(out_3));
endmodule

module FLIP_FLOP_D (
  input  D,
  input  CLOCK,
  output Q,
  output nQ
);

  wire nand_1_out, nand_2_out, not_1_out;

  not not_1 (not_1_out, D);
  nand nand_1 (nand_1_out, D, CLOCK);
  nand nand_2 (nand_2_out, not_1_out, CLOCK);
  nand nand_3 (Q, nand_1_out, nQ);
  nand nand_4 (nQ, Q, nand_2_out);
endmodule
