// Logisim project flip_flop_jk.circ as structural Verilog: 2 circuits, main circuit main
module main (
  input  J,
  input  CLOCK,
  input  K,
  output q,
  output minus_q
);

  wire button_1_out, nand_1_out, nand_2_out, nand_3_out, nand_4_out, nand_5_out, nand_6_out, not_1_out,
       not_2_out, not_3_out;

  not not_1 (not_1_out, CLOCK);
  nand nand_1 (nand_1_out, minus_q, J, not_1_out);
  nand nand_2 (nand_2_out, not_1_out, K, q);
  nand nand_3 (nand_3_out, nand_1_out, nand_4_out);
  nand nand_4 (nand_4_out, nand_3_out, not_3_out, nand_2_out);
  not not_2 (not_2_out, not_1_out);
  not not_3 (not_3_out, button_1_out);
  Button button_1 (.out(button_1_out));
  nand nand_5 (nand_5_out, nand_3_out, not_2_out);
  nand nand_6 (nand_6_out, not_2_out, nand_4_out);
  nand nand_7 (q, minus_q, nand_5_out);
  nand nand_8 (minus_q, nand_6_out, not_3_out, q);

  // Notes on the sheet:
  //   CLIQUE NO BOTÃO PARA INICIAR A SIMULAÇÃO
endmodule

module flip_flop_jk (
  input  J,
  input  CLOCK,
  input  K,
  output q,
  output minus_q
);

  wire button_1_out, nand_1_out, nand_2_out, nand_3_out, nand_4_out, nand_5_out, nand_6_out, not_1_out,
       not_2_out, not_3_out;

  not not_1 (not_1_out, CLOCK);
  nand nand_1 (nand_1_out, minus_q, J, not_1_out);
  nand nand_2 (nand_2_out, not_1_out, K, q);
  nand nand_3 (nand_3_out, nand_1_out, nand_4_out);
  nand nand_4 (nand_4_out, nand_3_out, not_3_out, nand_2_out);
  not not_2 (not_2_out, not_1_out);
  not not_3 (not_3_out, button_1_out);
  Button button_1 (.out(button_1_out));
  nand nand_5 (nand_5_out, nand_3_out, not_2_out);
  nand nand_6 (nand_6_out, not_2_out, nand_4_out);
  nand nand_7 (q, minus_q, nand_5_out);
  nand nand_8 (minus_q, nand_6_out, not_3_out, q);
endmodule
