// Logisim project full_adder.circ as structural Verilog: 2 circuits, main circuit main
module main (
  input  carryin,
  input  b,
  input  a,
  output S,
  output c_OUT
);

  full_adder full_adder_1 (.CARRY_OUT(c_OUT), .S(S), .A(a), .B(b), .CARRY_IN(carryin));
endmodule

module full_adder (
  input  A,
  input  B,
  input  CARRY_IN,
  output S,
  output CARRY_OUT
);

  wire and_1_out, and_2_out, xor_1_out;

  xor xor_1 (xor_1_out, A, B);
  and and_1 (and_1_out, CARRY_IN, xor_1_out);
  and and_2 (and_2_out, B, A);
  xor xor_2 (S, xor_1_out, CARRY_IN);
  or or_1 (CARRY_OUT, and_1_out, and_2_out);

  // Notes on the sheet:
  //   FULL ADDER
endmodule
