// Logisim project maquina_estados.circ as structural Verilog: 2 circuits, main circuit main
module main (
  input  in_1
);

  wire clock_1_out, \semaforo_1_saída ;

  semaforo semaforo_1 (.\SAÍDA (\semaforo_1_saída ), .CLOCK(clock_1_out), .ENTRADA(in_1));
  Clock clock_1 (.out(clock_1_out));
  LED led_1 (.in(\semaforo_1_saída ));
endmodule

module semaforo (
  input  CLOCK,
  input  ENTRADA,
  output \SAÍDA 
);

  wire and_1_out, and_2_out, or_1_out;

  and and_1 (and_1_out, ~\SAÍDA , ENTRADA);  // AND_Gate
  and and_2 (and_2_out, \SAÍDA , ~ENTRADA);  // AND_Gate
  or or_1 (or_1_out, and_1_out, and_2_out);
  D_Flip_Flop ESTADO_ATUAL (.clk(CLOCK), .D(or_1_out), .Q(\SAÍDA ));  // open: Qn, preset, en, reset
endmodule
