// Logisim project memoria_rom.circ as structural Verilog: 2 circuits, main circuit main
module main (
  input  [2:0] in_1,
  output [7:0] out_2
);

  ROM_memoria rom_memoria_1 (.in_1(in_1), .out_2(out_2));
endmodule

module ROM_memoria (
  input  [2:0] in_1,
  output [7:0] out_2
);

  wire and_1_out, and_2_out, and_3_out, and_4_out, and_5_out, and_6_out, and_7_out, and_8_out;

  and and_1 (and_1_out, ~in_1[2], ~in_1[1], ~in_1[0]);  // AND_Gate
  and and_2 (and_2_out, ~in_1[2], ~in_1[1], in_1[0]);  // AND_Gate
  and and_3 (and_3_out, ~in_1[2], in_1[1], ~in_1[0]);  // AND_Gate
  and and_4 (and_4_out, ~in_1[2], in_1[1], in_1[0]);  // AND_Gate
  and and_5 (and_5_out, in_1[2], ~in_1[1], ~in_1[0]);  // AND_Gate
  and and_6 (and_6_out, in_1[2], ~in_1[1], in_1[0]);  // AND_Gate
  and and_7 (and_7_out, in_1[2], in_1[1], ~in_1[0]);  // AND_Gate
  and and_8 (and_8_out, in_1[2], in_1[1], in_1[0]);
  or or_1 (out_2[0], and_1_out, and_3_out, and_6_out);
  buf or_2 (out_2[1], and_2_out);  // OR_Gate
  or or_3 (out_2[2], and_7_out, and_4_out, and_8_out);
  or or_4 (out_2[3], and_5_out, and_4_out);
  or or_5 (out_2[4], and_1_out, and_8_out);
  or or_6 (out_2[5], and_2_out, and_7_out);
  or or_7 (out_2[6], and_6_out, and_2_out);
  or or_8 (out_2[7], and_8_out, and_1_out);
endmodule
