// Logisim project multiplexador_4_1.circ as structural Verilog: 2 circuits, main circuit main
module main (
  input  E3,
  input  E2,
  input  E1,
  input  E0,
  input  s1,
  input  s2,
  output S
);

  MULTIPLEXADOR_4_1 multiplexador_4_1_1 (.E0(E0), .E2(E2), .E1(E1), .S0(s2), .E3(E3), .S1(s1), .S(S));

  // Notes on the sheet:
  //   multiplexador com 4 opções de entrada
endmodule

module MULTIPLEXADOR_4_1 (
  input  E0,
  input  E2,
  input  E1,
  input  S0,
  input  E3,
  input  S1,
  output S
);

  wire and_1_out, and_2_out, and_3_out, and_4_out, not_1_out, not_2_out;

  not not_1 (not_1_out, S1);
  not not_2 (not_2_out, S0);
  and and_1 (and_1_out, E0, not_2_out, not_1_out);
  and and_2 (and_2_out, E2, S0, not_1_out);
  and and_3 (and_3_out, E1, not_2_out, S1);
  and and_4 (and_4_out, E3, S0, S1);
  or or_1 (S, and_1_out, and_2_out, and_3_out, and_4_out);
endmodule
