// Logisim project otimizacao_logica.circ as structural Verilog: 1 circuit, main circuit main
module main (
  input  A,
  input  B,
  input  C,
  input  A_2,
  input  B_2,
  input  C_2
);

  wire and_1_out, and_2_out, and_3_out, and_4_out, or_1_out, or_2_out;

  and and_1 (and_1_out, B, C);
  and and_2 (and_2_out, A, B);
  and and_3 (and_3_out, ~B, C);  // AND_Gate
  and and_4 (and_4_out, A, ~B);  // AND_Gate
  _7_Segment_Display u_7_segment_display_1 (.c(or_1_out));  // open: g, f, a, b, e, d, dp
  or or_1 (or_1_out, ~B, and_1_out, and_2_out, and_3_out, and_4_out);  // OR_Gate
  or or_2 (or_2_out, A_2, ~B_2, C_2);  // OR_Gate
  _7_Segment_Display u_7_segment_display_2 (.c(or_2_out));  // open: g, f, a, b, e, d, dp

  // Notes on the sheet:
  //   EXPRESSÃO PARA ENTRADA C
  //   DE BINÁRIO PARA DECIMAL 7 SEGMENTOS
  //   EXPRESSÃO SIMPLIFICADA
endmodule
