// Logisim project pergunta_professor.circ as structural Verilog: 2 circuits, main circuit main
module main (
  input  [3:0] entrada
);
endmodule

module XOR_4BITS (
  input  [3:0] entrada,
  output out_2
);

  wire and_1_out, and_2_out, and_3_out, and_4_out, or_1_out, or_2_out;

  and and_1 (and_1_out, ~entrada[3], entrada[2]);  // AND_Gate
  and and_2 (and_2_out, entrada[3], ~entrada[2]);  // AND_Gate
  and and_3 (and_3_out, ~entrada[1], entrada[0]);  // AND_Gate
  and and_4 (and_4_out, entrada[1], ~entrada[0]);  // AND_Gate
  or or_1 (or_1_out, and_1_out, and_2_out);
  or or_2 (or_2_out, and_3_out, and_4_out);
  xor xor_1 (out_2, or_1_out, or_2_out);

  // Notes on the sheet:
  //   Para detectar uma paridade ímpar
  //   XOR de A e B
  //   XOR de C e D
  //   é necessário apenas um XOR com as entradas, pois a saída será 1
  //   se a quantidade de 1's da entrada for ímpar
  //   XOR DE A, B, C e D
endmodule
