// Logisim project ram.circ as structural Verilog: 3 circuits, main circuit main
module main (
  input  [7:0] in_1,
  input  [2:0] in_2,
  input  in_3,
  output [7:0] out_4
);

  wire clock_1_out;

  RAM ram_1 (.write(in_1), .\saída (out_4), .clock(clock_1_out), .clear(in_3), .seletor(in_2));
  Clock clock_1 (.out(clock_1_out));
endmodule

// palavra
module memoria_valor (
  input  clock,
  input  [7:0] write,
  input  clear,
  output [7:0] \saída 
);

  wire [7:0] multiplexer_1_out;

  Multiplexer #(.width(8)) multiplexer_1 (
    .in0(write), .in1({8{1'b0}}), .out(multiplexer_1_out), .sel(clear));  // open: en
  D_Flip_Flop d_ff_1 (.clk(clock), .D(multiplexer_1_out[0]), .Q(\saída [0]));  // open: Qn, preset, en, reset
  D_Flip_Flop d_ff_2 (.clk(clock), .D(multiplexer_1_out[1]), .Q(\saída [1]));  // open: Qn, preset, en, reset
  D_Flip_Flop d_ff_3 (.clk(clock), .D(multiplexer_1_out[2]), .Q(\saída [2]));  // open: Qn, preset, en, reset
  D_Flip_Flop d_ff_4 (.clk(clock), .D(multiplexer_1_out[3]), .Q(\saída [3]));  // open: Qn, preset, en, reset
  D_Flip_Flop d_ff_5 (.clk(clock), .D(multiplexer_1_out[4]), .Q(\saída [4]));  // open: Qn, preset, en, reset
  D_Flip_Flop d_ff_6 (.clk(clock), .D(multiplexer_1_out[5]), .Q(\saída [5]));  // open: Qn, preset, en, reset
  D_Flip_Flop d_ff_7 (.clk(clock), .D(multiplexer_1_out[6]), .Q(\saída [6]));  // open: Qn, preset, en, reset
  D_Flip_Flop d_ff_8 (.clk(clock), .D(multiplexer_1_out[7]), .Q(\saída [7]));  // open: Qn, preset, en, reset
endmodule

module RAM (
  input  [2:0] seletor,
  input  clear,
  input  clock,
  input  [7:0] write,
  output [7:0] \saída 
);

  wire demultiplexer_1_out0, demultiplexer_1_out1, demultiplexer_1_out2, demultiplexer_1_out3,
       demultiplexer_1_out4, demultiplexer_1_out5, demultiplexer_1_out6, demultiplexer_1_out7;
  wire [7:0] demultiplexer_2_out0, demultiplexer_2_out1, demultiplexer_2_out2, demultiplexer_2_out3,
       demultiplexer_2_out4, demultiplexer_2_out5, demultiplexer_2_out6, demultiplexer_2_out7,
       \memoria_valor_1_saída , \memoria_valor_2_saída , \memoria_valor_3_saída , \memoria_valor_4_saída ,
       \memoria_valor_5_saída , \memoria_valor_6_saída , \memoria_valor_7_saída , \memoria_valor_8_saída ;

  Demultiplexer #(.select(3)) demultiplexer_1 (
    .out0(demultiplexer_1_out0), .out1(demultiplexer_1_out1), .out2(demultiplexer_1_out2),
    .out3(demultiplexer_1_out3), .out4(demultiplexer_1_out4), .out5(demultiplexer_1_out5),
    .out6(demultiplexer_1_out6), .out7(demultiplexer_1_out7), .in(clock), .sel(seletor));  // open: en
  Demultiplexer #(.select(3), .width(8)) demultiplexer_2 (
    .out0(demultiplexer_2_out0), .out1(demultiplexer_2_out1), .out2(demultiplexer_2_out2),
    .out3(demultiplexer_2_out3), .out4(demultiplexer_2_out4), .out5(demultiplexer_2_out5),
    .out6(demultiplexer_2_out6), .out7(demultiplexer_2_out7), .in(write), .sel(seletor));  // open: en
  memoria_valor memoria_valor_1 (
    .write(demultiplexer_2_out0), .\saída (\memoria_valor_1_saída ), .clock(demultiplexer_1_out0),
    .clear(clear));
  memoria_valor memoria_valor_2 (
    .write(demultiplexer_2_out1), .\saída (\memoria_valor_2_saída ), .clock(demultiplexer_1_out1),
    .clear(clear));
  memoria_valor memoria_valor_3 (
    .write(demultiplexer_2_out2), .\saída (\memoria_valor_3_saída ), .clock(demultiplexer_1_out2),
    .clear(clear));
  memoria_valor memoria_valor_4 (
    .write(demultiplexer_2_out3), .\saída (\memoria_valor_4_saída ), .clock(demultiplexer_1_out3),
    .clear(clear));
  memoria_valor memoria_valor_5 (
    .write(demultiplexer_2_out4), .\saída (\memoria_valor_5_saída ), .clock(demultiplexer_1_out4),
    .clear(clear));
  memoria_valor memoria_valor_6 (
    .write(demultiplexer_2_out5), .\saída (\memoria_valor_6_saída ), .clock(demultiplexer_1_out5),
    .clear(clear));
  memoria_valor memoria_valor_7 (
    .write(demultiplexer_2_out6), .\saída (\memoria_valor_7_saída ), .clock(demultiplexer_1_out6),
    .clear(clear));
  memoria_valor memoria_valor_8 (
    .write(demultiplexer_2_out7), .\saída (\memoria_valor_8_saída ), .clock(demultiplexer_1_out7),
    .clear(clear));
  Multiplexer #(.select(3), .width(8)) multiplexer_1 (
    .in0(\memoria_valor_1_saída ), .in1(\memoria_valor_2_saída ), .in2(\memoria_valor_3_saída ),
    .in3(\memoria_valor_4_saída ), .in4(\memoria_valor_5_saída ), .in5(\memoria_valor_6_saída ),
    .in6(\memoria_valor_7_saída ), .in7(\memoria_valor_8_saída ), .out(\saída ), .sel(seletor));  // open: en
endmodule
