// Logisim project registrador.circ as structural Verilog: 2 circuits, main circuit main
module main (
  input  [7:0] in_1,
  output [7:0] out_2
);

  registrador registrador_1 (.entrada(in_1), .\saída (out_2));  // open: CLOCK
  Clock clock_1 ();  // open: out
endmodule

module registrador (
  input  [7:0] entrada,
  input  CLOCK,
  output [7:0] \saída 
);

  D_Flip_Flop d_ff_1 (.clk(CLOCK), .D(entrada[7]), .Q(\saída [7]));  // open: Qn, preset, en, reset
  D_Flip_Flop d_ff_2 (.clk(CLOCK), .D(entrada[6]), .Q(\saída [6]));  // open: Qn, preset, en, reset
  D_Flip_Flop d_ff_3 (.clk(CLOCK), .D(entrada[5]), .Q(\saída [5]));  // open: Qn, preset, en, reset
  D_Flip_Flop d_ff_4 (.clk(CLOCK), .D(entrada[4]), .Q(\saída [4]));  // open: Qn, preset, en, reset
  D_Flip_Flop d_ff_5 (.clk(CLOCK), .D(entrada[3]), .Q(\saída [3]));  // open: Qn, preset, en, reset
  D_Flip_Flop d_ff_6 (.clk(CLOCK), .D(entrada[2]), .Q(\saída [2]));  // open: Qn, preset, en, reset
  D_Flip_Flop d_ff_7 (.clk(CLOCK), .D(entrada[1]), .Q(\saída [1]));  // open: Qn, preset, en, reset
  D_Flip_Flop d_ff_8 (.clk(CLOCK), .D(entrada[0]), .Q(\saída [0]));  // open: Qn, preset, en, reset
endmodule
