// Logisim project shift.circ as structural Verilog: 2 circuits, main circuit main
module main (
  input  [7:0] in_1,
  input  in_2,
  output [7:0] out_3
);

  shift_2 shift_2_1 (.\saída (out_3), .\direção (in_2), .entrada(in_1));
endmodule

module shift_2 (
  input  \direção ,
  input  [7:0] entrada,
  output [7:0] \saída 
);

  Multiplexer #(.width(8)) multiplexer_1 (
    .in0({entrada[5:0], 2'b00}), .in1({2'b00, entrada[7:2]}), .out(\saída ), .sel(\direção ));  // open: en
endmodule
