// Logisim project somador_8_bits.circ as structural Verilog: 2 circuits, main circuit main
module main (
  input  [7:0] A,
  input  [7:0] B,
  output out_3,
  output [7:0] S
);

  somador_8_bits somador_8_bits_1 (.A(A), .B(B), .S(S), .overflow(out_3));
endmodule

module somador_8_bits (
  input  [7:0] A,
  input  [7:0] B,
  output [7:0] S,
  output overflow
);

  wire full_adder_1_carry_out, full_adder_2_carry_out, full_adder_3_carry_out, full_adder_4_carry_out,
       full_adder_5_carry_out, full_adder_6_carry_out, full_adder_7_carry_out;

  full_adder full_adder_1 (.CARRY_OUT(full_adder_1_carry_out), .S(S[0]), .A(A[0]), .B(B[0]), .CARRY_IN(1'b0));
  full_adder full_adder_2 (
    .CARRY_OUT(full_adder_2_carry_out), .S(S[1]), .A(A[1]), .B(B[1]), .CARRY_IN(full_adder_1_carry_out));
  full_adder full_adder_3 (
    .CARRY_OUT(full_adder_3_carry_out), .S(S[2]), .A(A[2]), .B(B[2]), .CARRY_IN(full_adder_2_carry_out));
  full_adder full_adder_4 (
    .CARRY_OUT(full_adder_4_carry_out), .S(S[3]), .A(A[3]), .B(B[3]), .CARRY_IN(full_adder_3_carry_out));
  full_adder full_adder_5 (
    .CARRY_OUT(full_adder_5_carry_out), .S(S[4]), .A(A[4]), .B(B[4]), .CARRY_IN(full_adder_4_carry_out));
  full_adder full_adder_6 (
    .CARRY_OUT(full_adder_6_carry_out), .S(S[5]), .A(A[5]), .B(B[5]), .CARRY_IN(full_adder_5_carry_out));
  full_adder full_adder_7 (
    .CARRY_OUT(full_adder_7_carry_out), .S(S[6]), .A(A[6]), .B(B[6]), .CARRY_IN(full_adder_6_carry_out));
  full_adder full_adder_8 (.CARRY_OUT(overflow), .S(S[7]), .A(A[7]), .B(B[7]), .CARRY_IN(full_adder_7_carry_out));
endmodule
