// Logisim project somador_8_bits_mais_4.circ as structural Verilog: 2 circuits, main circuit main
module main (
  input  [7:0] in_1,
  output [8:0] out_2
);

  somador_8b_mais_4 somador_8b_mais_4_1 (.\Saída (out_2), .\A_será_somado_com_4 (in_1));
endmodule

module somador_8b_mais_4 (
  input  [7:0] \A_será_somado_com_4 ,
  output [8:0] \Saída 
);

  wire full_adder_1_carry_out, full_adder_2_carry_out, full_adder_3_carry_out, full_adder_4_carry_out,
       full_adder_5_carry_out, full_adder_6_carry_out, full_adder_7_carry_out;

  full_adder full_adder_1 (
    .CARRY_OUT(full_adder_1_carry_out), .S(\Saída [0]), .A(\A_será_somado_com_4 [0]), .B(1'b0),
    .CARRY_IN(1'b0));
  full_adder full_adder_2 (
    .CARRY_OUT(full_adder_2_carry_out), .S(\Saída [1]), .A(\A_será_somado_com_4 [1]), .B(1'b0),
    .CARRY_IN(full_adder_1_carry_out));
  full_adder full_adder_3 (
    .CARRY_OUT(full_adder_3_carry_out), .S(\Saída [2]), .A(\A_será_somado_com_4 [2]), .B(1'b1),
    .CARRY_IN(full_adder_2_carry_out));
  full_adder full_adder_4 (
    .CARRY_OUT(full_adder_4_carry_out), .S(\Saída [3]), .A(\A_será_somado_com_4 [3]), .B(1'b0),
    .CARRY_IN(full_adder_3_carry_out));
  full_adder full_adder_5 (
    .CARRY_OUT(full_adder_5_carry_out), .S(\Saída [4]), .A(\A_será_somado_com_4 [4]), .B(1'b0),
    .CARRY_IN(full_adder_4_carry_out));
  full_adder full_adder_6 (
    .CARRY_OUT(full_adder_6_carry_out), .S(\Saída [5]), .A(\A_será_somado_com_4 [5]), .B(1'b0),
    .CARRY_IN(full_adder_5_carry_out));
  full_adder full_adder_7 (
    .CARRY_OUT(full_adder_7_carry_out), .S(\Saída [6]), .A(\A_será_somado_com_4 [6]), .B(1'b0),
    .CARRY_IN(full_adder_6_carry_out));
  full_adder full_adder_8 (
    .CARRY_OUT(\Saída [8]), .S(\Saída [7]), .A(\A_será_somado_com_4 [7]), .B(1'b0),
    .CARRY_IN(full_adder_7_carry_out));
endmodule
