// Logisim project subtrator_8_BITS.circ as structural Verilog: 3 circuits, main circuit main
module main (
  input  [7:0] in_1,
  input  [7:0] in_2,
  output [7:0] out_3,
  output out_4
);

  subtrator subtrator_1 (.\SAÍDA (out_3), .OVERFLOW(out_4), .A(in_1), .B(in_2));
endmodule

module subtracao (
  input  A,
  input  B,
  input  CARRY_IN,
  output D,
  output CARRY_OUT
);

  wire and_1_out, and_2_out, and_3_out, not_1_out, xor_1_out;

  not not_1 (not_1_out, A);
  and and_1 (and_1_out, not_1_out, CARRY_IN);
  xor xor_1 (xor_1_out, A, B);
  and and_2 (and_2_out, B, not_1_out);
  and and_3 (and_3_out, B, CARRY_IN);
  xor xor_2 (D, xor_1_out, CARRY_IN);
  or or_1 (CARRY_OUT, and_2_out, and_3_out, and_1_out);
endmodule

module subtrator (
  input  [7:0] A,
  input  [7:0] B,
  output [7:0] \SAÍDA ,
  output OVERFLOW
);

  wire subtracao_1_carry_out, subtracao_2_carry_out, subtracao_3_carry_out, subtracao_4_carry_out,
       subtracao_5_carry_out, subtracao_6_carry_out, subtracao_7_carry_out;

  subtracao subtracao_1 (.A(A[0]), .B(B[0]), .CARRY_IN(1'b0), .D(\SAÍDA [0]), .CARRY_OUT(subtracao_1_carry_out));
  subtracao subtracao_2 (
    .A(A[1]), .B(B[1]), .CARRY_IN(subtracao_1_carry_out), .D(\SAÍDA [1]), .CARRY_OUT(subtracao_2_carry_out));
  subtracao subtracao_3 (
    .A(A[2]), .B(B[2]), .CARRY_IN(subtracao_2_carry_out), .D(\SAÍDA [2]), .CARRY_OUT(subtracao_3_carry_out));
  subtracao subtracao_4 (
    .A(A[3]), .B(B[3]), .CARRY_IN(subtracao_3_carry_out), .D(\SAÍDA [3]), .CARRY_OUT(subtracao_4_carry_out));
  subtracao subtracao_5 (
    .A(A[4]), .B(B[4]), .CARRY_IN(subtracao_4_carry_out), .D(\SAÍDA [4]), .CARRY_OUT(subtracao_5_carry_out));
  subtracao subtracao_6 (
    .A(A[5]), .B(B[5]), .CARRY_IN(subtracao_5_carry_out), .D(\SAÍDA [5]), .CARRY_OUT(subtracao_6_carry_out));
  subtracao subtracao_7 (
    .A(A[6]), .B(B[6]), .CARRY_IN(subtracao_6_carry_out), .D(\SAÍDA [6]), .CARRY_OUT(subtracao_7_carry_out));
  subtracao subtracao_8 (.A(A[7]), .B(B[7]), .CARRY_IN(subtracao_7_carry_out), .D(\SAÍDA [7]), .CARRY_OUT(OVERFLOW));
endmodule
