// Logisim project xor.circ as structural Verilog: 2 circuits, main circuit main
module main (
  input  in_1,
  input  in_2,
  output out_3
);

  \xor  xor_1 (.b(in_1), .a(in_2), .s(out_3));

  // Notes on the sheet:
  //   xor usando and, not e or
endmodule

module \xor  (
  input  b,
  input  a,
  output s
);

  wire and_1_out, and_2_out, not_1_out, not_2_out;

  not not_1 (not_1_out, a);
  not not_2 (not_2_out, b);
  and and_1 (and_1_out, not_1_out, b);
  and and_2 (and_2_out, a, not_2_out);
  or or_1 (s, and_1_out, and_2_out);

  // Notes on the sheet:
  //   A⊕B=¬A⋅B+A⋅¬B
  //   a b s
  //   0 0 0
  //   0 1 1
  //   1 0 1
  //   1 1 0
endmodule
